# Fritzing sketch fys_project (saved by Fritzing 0.9.10b)
breadboards: 1

parts:
  Part1 = ODROID-N2Plus [part_number="ODROID N2Plus"]
  J1 = Basic Servo
  HC-SR04_Sensor_1 = HC-SR04 Ultrasonic Distance Sensor
  SOUND_SENSOR = Dagu DGServo 9g header connector (female) [package=THT]
  Mod1 = KY-008 Laser Transmitter Module [package="Breakout board"]
  Mod2 = KY-018 Photoresistor Module [package="Breakout board"]

nets:
  N1: Part1.connector1, Mod2.Vin
  VCC: Part1.connector2, J1.vcc, HC-SR04_Sensor_1.VCC, SOUND_SENSOR.Vcc, Mod1.S
  GND: Part1.connector6, J1.gnd, HC-SR04_Sensor_1.GND, SOUND_SENSOR.gnd, Mod1.NC, Mod1.-, Mod2.-
  N2: Part1.connector7, HC-SR04_Sensor_1.TRIG
  N3: Part1.connector10, Part1.connector12, Part1.connector14, Part1.connector16, Part1.connector18, J1.pulse
  N4: Part1.connector11, HC-SR04_Sensor_1.ECHO
  N5: Part1.connector35, Mod2.S
  N6: Part1.connector37, SOUND_SENSOR.pulse

custom parts:
  KY-008 Laser Transmitter Module: KY-008 Laser Transmitter Module, emits a dot shaped red laser beam.
  KY-018 Photoresistor Module: KY-018 Photoresistor module, used to measure light intensity. It can determine the presence or absence of light.
